// Logisim project boolean-xor.circ as structural Verilog: 1 circuit, main circuit main
module main (
  input  A,
  input  B,
  output DNF,
  output CNF
);

  wire and_1_out, and_2_out, nA, nB, or_1_out, or_2_out;

  not not_1 (nA, A);
  not not_2 (nB, B);
  and and_1 (and_1_out, nA, B);
  and and_2 (and_2_out, A, nB);
  or or_1 (or_1_out, A, B);
  or or_2 (or_2_out, nA, nB);
  or or_3 (DNF, and_1_out, and_2_out);
  and and_3 (CNF, or_1_out, or_2_out);

  // Notes on the sheet:
  //   DNF
  //   CNF
endmodule
