// Logisim project cmos-inverter.circ as structural Verilog: 1 circuit, main circuit main
module main (
  input  A,
  output Y
);

  Transistor #(.\type ("p"), .gate("tl")) transistor_1 (.in(1'b1), .out(Y), .gate(A));
  Transistor #(.\type ("n"), .gate("tl")) transistor_2 (.in(1'b0), .out(Y), .gate(A));
endmodule
