// Logisim project cmos-nor.circ as structural Verilog: 1 circuit, main circuit main
module main (
  input  A,
  input  B,
  output Y
);

  wire transistor_1_out;

  Transistor #(.\type ("p"), .gate("tl")) transistor_1 (.in(1'b1), .out(transistor_1_out), .gate(A));
  Transistor #(.\type ("p"), .gate("tl")) transistor_2 (.in(transistor_1_out), .out(Y), .gate(B));
  Transistor #(.\type ("n"), .gate("tl")) transistor_3 (.in(1'b0), .out(Y), .gate(A));
  Transistor #(.\type ("n"), .gate("br")) transistor_4 (.in(1'b0), .out(Y), .gate(B));
endmodule
