// Logisim project decoder.circ as structural Verilog: 1 circuit, main circuit main
module main (
  input  [3:0] A,
  output Out0,
  output Out1,
  output Out2,
  output Out3,
  output Out4,
  output Out5,
  output Out6,
  output Out7,
  output Out8,
  output Out9,
  output Out10,
  output Out11,
  output Out12,
  output Out13,
  output Out14,
  output Out15
);

  Decoder #(.select(4), .enable("false")) decoder_1 (
    .out0(Out0), .out1(Out1), .out2(Out2), .out3(Out3), .out4(Out4), .out5(Out5), .out6(Out6), .out7(Out7),
    .out8(Out8), .out9(Out9), .out10(Out10), .out11(Out11), .out12(Out12), .out13(Out13), .out14(Out14),
    .out15(Out15), .sel(A));
endmodule
