// Logisim project demultiplexer.circ as structural Verilog: 1 circuit, main circuit main
module main (
  input  DI,
  input  [2:0] Sel,
  output Out0,
  output Out1,
  output Out2,
  output Out3,
  output Out4,
  output Out5,
  output Out6,
  output Out7
);

  Demultiplexer #(.select(3), .enable("false")) demultiplexer_1 (
    .out0(Out0), .out1(Out1), .out2(Out2), .out3(Out3), .out4(Out4), .out5(Out5), .out6(Out6), .out7(Out7),
    .in(DI), .sel(Sel));
endmodule
