// Logisim project full-adder.circ as structural Verilog: 1 circuit, main circuit main
module main (
  input  A,
  input  B,
  input  Cin,
  output Sum,
  output Cout
);

  wire and_1_out, and_2_out, P;

  xor xor_1 (P, A, B);
  and and_1 (and_1_out, A, B);
  and and_2 (and_2_out, P, Cin);
  xor xor_2 (Sum, P, Cin);
  or or_1 (Cout, and_1_out, and_2_out);
endmodule
