// Logisim project mini-alu.circ as structural Verilog: 1 circuit, main circuit main
module main (
  input  [7:0] A,
  input  [7:0] B,
  input  [2:0] Sel,
  output [7:0] Out
);

  wire [7:0] Op0, Op1, Op2, Op3, Op4, Op5, Op6, Op7;

  Adder #(.width(8)) adder_1 (.a(A), .b(B), .out(Op0), .cin(1'b0));  // open: cout
  assign Op2 = A & B;  // AND_Gate and_1, 8 bits wide
  assign Op4 = A ^ B;  // XOR_Gate xor_1, 8 bits wide
  Shifter #(.width(8), .shift("lr")) shifter_1 (.in(A), .\dist (B[2:0]), .out(Op6));
  Subtractor #(.width(8)) subtractor_1 (.a(A), .b(B), .out(Op1), .bin(1'b0));  // open: bout
  assign Op3 = A | B;  // OR_Gate or_1, 8 bits wide
  Shifter #(.width(8), .shift("ll")) shifter_2 (.in(A), .\dist (B[2:0]), .out(Op5));
  Shifter #(.width(8), .shift("ll")) shifter_3 (.in(A), .\dist (B[2:0]), .out(Op7));
  Multiplexer #(.select(3), .enable("false"), .width(8)) multiplexer_1 (
    .in0(Op0), .in1(Op1), .in2(Op2), .in3(Op3), .in4(Op4), .in5(Op5), .in6(Op6), .in7(Op7), .out(Out),
    .sel(Sel));

  // Other names for the same wires on the sheet: Shift[2:0] = B[2:0]

  // Notes on the sheet:
  //   0  ADD
  //   2  AND
  //   4  XOR
  //   6  LSR
  //   1  SUB
  //   3  OR
  //   5  LSL
  //   7  ASL
endmodule
