// Logisim project multiplexer.circ as structural Verilog: 1 circuit, main circuit main
module main (
  input  A0,
  input  A1,
  input  A2,
  input  A3,
  input  A4,
  input  A5,
  input  A6,
  input  A7,
  input  [2:0] Sel,
  output Out
);

  Multiplexer #(.select(3), .enable("false")) multiplexer_1 (
    .in0(A0), .in1(A1), .in2(A2), .in3(A3), .in4(A4), .in5(A5), .in6(A6), .in7(A7), .out(Out), .sel(Sel));
endmodule
