// Logisim project multiply-4bit.circ as structural Verilog: 1 circuit, main circuit main
module main (
  input  [3:0] A,
  input  [3:0] B,
  output [7:0] Product
);

  wire [3:0] and_1_out, and_2_out, and_3_out, and_4_out, bit_extender_1_out, bit_extender_2_out,
       bit_extender_3_out, bit_extender_4_out;
  wire [7:0] bit_extender_5_out, bit_extender_6_out, bit_extender_7_out, bit_extender_8_out, P0, P1, P2, P3,
       T0, T1;

  assign bit_extender_1_out = {{3{B[0]}}, B[0]};  // Bit_Extender bit_extender_1
  assign bit_extender_2_out = {{3{B[1]}}, B[1]};  // Bit_Extender bit_extender_2
  assign bit_extender_3_out = {{3{B[2]}}, B[2]};  // Bit_Extender bit_extender_3
  assign bit_extender_4_out = {{3{B[3]}}, B[3]};  // Bit_Extender bit_extender_4
  assign and_1_out = A & bit_extender_1_out;  // AND_Gate and_1, 4 bits wide
  assign and_2_out = A & bit_extender_2_out;  // AND_Gate and_2, 4 bits wide
  assign and_3_out = A & bit_extender_3_out;  // AND_Gate and_3, 4 bits wide
  assign and_4_out = A & bit_extender_4_out;  // AND_Gate and_4, 4 bits wide
  assign bit_extender_5_out = {{4{1'b0}}, and_1_out};  // Bit_Extender bit_extender_5
  Shifter #(.width(8), .shift("ll")) shifter_1 (.in(bit_extender_5_out), .\dist (3'b000), .out(P0));
  assign bit_extender_6_out = {{4{1'b0}}, and_2_out};  // Bit_Extender bit_extender_6
  Shifter #(.width(8), .shift("ll")) shifter_2 (.in(bit_extender_6_out), .\dist (3'b001), .out(P1));
  assign bit_extender_7_out = {{4{1'b0}}, and_3_out};  // Bit_Extender bit_extender_7
  Shifter #(.width(8), .shift("ll")) shifter_3 (.in(bit_extender_7_out), .\dist (3'b010), .out(P2));
  assign bit_extender_8_out = {{4{1'b0}}, and_4_out};  // Bit_Extender bit_extender_8
  Shifter #(.width(8), .shift("ll")) shifter_4 (.in(bit_extender_8_out), .\dist (3'b011), .out(P3));
  Adder #(.width(8)) adder_1 (.a(P0), .b(P1), .out(T0), .cin(1'b0));  // open: cout
  Adder #(.width(8)) adder_2 (.a(P2), .b(P3), .out(T1), .cin(1'b0));  // open: cout
  Adder #(.width(8)) adder_3 (.a(T0), .b(T1), .out(Product), .cin(1'b0));  // open: cout
endmodule
