// Logisim project shifts-8bit.circ as structural Verilog: 1 circuit, main circuit main
module main (
  input  [7:0] A,
  input  [2:0] Shift,
  output [7:0] LSL,
  output [7:0] LSR,
  output [7:0] ASR,
  output [7:0] ROL,
  output [7:0] ROR
);

  Shifter #(.width(8), .shift("ll")) shifter_1 (.in(A), .\dist (Shift), .out(LSL));
  Shifter #(.width(8), .shift("lr")) shifter_2 (.in(A), .\dist (Shift), .out(LSR));
  Shifter #(.width(8), .shift("ar")) shifter_3 (.in(A), .\dist (Shift), .out(ASR));
  Shifter #(.width(8), .shift("rl")) shifter_4 (.in(A), .\dist (Shift), .out(ROL));
  Shifter #(.width(8), .shift("rr")) shifter_5 (.in(A), .\dist (Shift), .out(ROR));
endmodule
