// Logisim project subtract-8bit.circ as structural Verilog: 3 circuits, main circuit main
module main (
  input  [7:0] A,
  input  [7:0] B,
  output [7:0] Difference,
  output Borrow
);

  wire add8_1_cout;
  wire [7:0] not_1_out;

  assign not_1_out = ~B;  // NOT_Gate not_1, 8 bits wide
  ADD8 add8_1 (.A(A), .B(not_1_out), .Cin(1'b1), .Sum(Difference), .Cout(add8_1_cout));
  not not_2 (Borrow, add8_1_cout);
endmodule

module ADD8 (
  input  [7:0] A,
  input  [7:0] B,
  input  Cin,
  output [7:0] Sum,
  output Cout
);

  wire C4, fa1_1_cout, fa1_2_cout, fa1_3_cout, fa1_4_cout, fa1_5_cout, fa1_6_cout;

  FA1 fa1_1 (.A(A[0]), .B(B[0]), .Cin(Cin), .Sum(Sum[0]), .Cout(fa1_1_cout));
  FA1 fa1_2 (.A(A[4]), .B(B[4]), .Cin(C4), .Sum(Sum[4]), .Cout(fa1_2_cout));
  FA1 fa1_3 (.A(A[1]), .B(B[1]), .Cin(fa1_1_cout), .Sum(Sum[1]), .Cout(fa1_3_cout));
  FA1 fa1_4 (.A(A[5]), .B(B[5]), .Cin(fa1_2_cout), .Sum(Sum[5]), .Cout(fa1_4_cout));
  FA1 fa1_5 (.A(A[2]), .B(B[2]), .Cin(fa1_3_cout), .Sum(Sum[2]), .Cout(fa1_5_cout));
  FA1 fa1_6 (.A(A[6]), .B(B[6]), .Cin(fa1_4_cout), .Sum(Sum[6]), .Cout(fa1_6_cout));
  FA1 fa1_7 (.A(A[3]), .B(B[3]), .Cin(fa1_5_cout), .Sum(Sum[3]), .Cout(C4));
  FA1 fa1_8 (.A(A[7]), .B(B[7]), .Cin(fa1_6_cout), .Sum(Sum[7]), .Cout(Cout));

  // Other names for the same wires on the sheet: C0 = Cin; C8 = Cout; S0 = Sum[0]; S1 = Sum[1]; S2 = Sum[2];
  //   S3 = Sum[3]; S4 = Sum[4]; S5 = Sum[5]; S6 = Sum[6]; S7 = Sum[7]

  // Notes on the sheet:
  //   Bit 0
  //   Bit 4
  //   Bit 1
  //   Bit 5
  //   Bit 2
  //   Bit 6
  //   Bit 3
  //   Bit 7
endmodule

module FA1 (
  input  A,
  input  B,
  input  Cin,
  output Sum,
  output Cout
);

  wire and_1_out, and_2_out, P;

  xor xor_1 (P, A, B);
  and and_1 (and_1_out, A, B);
  and and_2 (and_2_out, P, Cin);
  xor xor_2 (Sum, P, Cin);
  or or_1 (Cout, and_1_out, and_2_out);
endmodule
